// Logisim project alu.circ as structural Verilog: 9 circuits, main circuit main
module main (
  input  [15:0] X,
  input  [15:0] Y,
  input  [3:0] switch__S,
  output signed_overflow,
  output [15:0] result,
  output equal
);

  wire and_2_out, and_3_out, and_4_out, and_5_out, comparator_1_eq, comparator_1_gt, comparator_1_lt,
       comparator_2_gt, comparator_2_lt, comparator_3_gt, comparator_3_lt, comparator_4_gt, comparator_4_lt,
       comparator_5_eq, comparator_6_eq, comparator_7_lt, or_1_out;
  wire [15:0] add, and_out, bc, ffo, lui, multiplexer_1_out, or_2_out, shifter_1_out, shifter_2_out,
       shifter_3_out, sub, zb;

  Comparator #(.width(16)) comparator_1 (
    .a(X), .b({16{1'b0}}), .gt(comparator_1_gt), .eq(comparator_1_eq), .lt(comparator_1_lt));
  Comparator #(.width(16)) comparator_2 (
    .a(Y), .b({16{1'b0}}), .gt(comparator_2_gt), .lt(comparator_2_lt));  // open: eq
  Comparator #(.width(16)) comparator_3 (
    .a(add), .b({16{1'b0}}), .gt(comparator_3_gt), .lt(comparator_3_lt));  // open: eq
  Comparator #(.width(16)) comparator_4 (
    .a(sub), .b({16{1'b0}}), .gt(comparator_4_gt), .lt(comparator_4_lt));  // open: eq
  Comparator #(.width(4)) comparator_5 (.a(switch__S), .b(4'b0110), .eq(comparator_5_eq));  // open: gt, lt
  Comparator #(.width(4)) comparator_6 (.a(switch__S), .b(4'b0111), .eq(comparator_6_eq));  // open: gt, lt
  or or_1 (or_1_out, comparator_1_gt, comparator_1_eq);
  Comparator #(.width(16)) comparator_7 (.a(X), .b(Y), .lt(comparator_7_lt));  // open: gt, eq
  assign and_out = X & Y;  // AND_Gate and, 16 bits wide
  assign or_2_out = X | Y;  // OR_Gate or_2, 16 bits wide
  Multiplexer #(.width(16)) multiplexer_1 (
    .in0({16{1'b0}}), .in1(16'h1), .out(multiplexer_1_out), .sel(comparator_7_lt));  // open: en
  Shifter #(.width(16)) shifter_1 (.in(X), .\dist (Y[3:0]), .out(shifter_1_out));
  Shifter #(.width(16), .shift("lr")) shifter_2 (.in(X), .\dist (Y[3:0]), .out(shifter_2_out));
  Shifter #(.width(16), .shift("ar")) shifter_3 (.in(X), .\dist (Y[3:0]), .out(shifter_3_out));
  Adder #(.width(16)) adder_1 (.a(X), .b(Y), .out(add));  // open: cin, cout
  Subtractor #(.width(16)) subtractor_1 (.a(X), .b(Y), .out(sub));  // open: bin, bout
  Comparator #(.width(16)) comparator_8 (.a(X), .b(Y), .eq(equal));  // open: gt, lt
  and and_2 (and_2_out, comparator_1_gt, comparator_2_gt, comparator_3_lt, comparator_5_eq);
  and and_3 (and_3_out, comparator_2_lt, comparator_3_gt, comparator_1_lt, comparator_5_eq);
  or or_3 (signed_overflow, and_2_out, and_3_out, and_4_out, and_5_out);
  and and_4 (and_4_out, or_1_out, comparator_2_lt, comparator_6_eq, comparator_4_lt);
  and and_5 (and_5_out, comparator_1_lt, comparator_2_gt, comparator_4_gt, comparator_6_eq);
  Multiplexer #(.select(4), .width(16)) multiplexer_2 (
    .in0(and_out), .in1(or_2_out), .in2(multiplexer_1_out), .in3(shifter_1_out), .in4(shifter_2_out),
    .in5(shifter_3_out), .in6(add), .in7(sub), .in8(ffo), .in9(zb), .in10(bc), .in11(X), .in12(lui),
    .out(result), .sel(switch__S));  // open: in13, in14, in15, en
  ffo u_ffo (.rs(X), .out(ffo));
  zb u_zb (.rs(X), .out(zb));
  bc u_bc (.rs(X), .out(bc));
  Shifter #(.width(16)) shifter_4 (.in(Y), .\dist (4'b1000), .out(lui));

  // Other names for the same wires on the sheet: j[15:0] = X; S[3:0] = switch__S

  // Notes on the sheet:
  //   These are INPUTS to your circuit
  //   This is an INPUT to your circuit
  //   DO NOT CHANGE THE LOCATIONS OF THE INPUTS/OUTPUTS! IF YOU DO SO, YOU NEED TO MAKE SURE THE PINS ARE AT THE RIGHT PLACE!
  //   These are OUTPUTS to your circuit
endmodule

module ffo (
  input  [15:0] rs,
  output [15:0] out
);

  wire bitfinder_1_found;
  wire [3:0] bitfinder_1_index;
  wire [15:0] bit_extender_1_out, subtractor_1_out;

  BitFinder #(.width(16), .\type ("high1")) bitfinder_1 (.in(rs), .index(bitfinder_1_index), .found(bitfinder_1_found));
  assign bit_extender_1_out = {{12{1'b0}}, bitfinder_1_index};  // Bit_Extender bit_extender_1
  Subtractor #(.width(16)) subtractor_1 (.a(16'hf), .b(bit_extender_1_out), .out(subtractor_1_out));  // open: bin, bout
  Multiplexer #(.width(16)) multiplexer_1 (
    .in0(16'h10), .in1(subtractor_1_out), .out(out), .sel(bitfinder_1_found));  // open: en
endmodule

module zb (
  input  [15:0] rs,
  output [15:0] out
);

  wire comparator_1_eq, comparator_2_eq, or_1_out;

  Comparator comparator_1 (.a(rs[7:0]), .b({8{1'b0}}), .eq(comparator_1_eq));  // open: gt, lt
  Comparator comparator_2 (.a(rs[15:8]), .b({8{1'b0}}), .eq(comparator_2_eq));  // open: gt, lt
  or or_1 (or_1_out, comparator_1_eq, comparator_2_eq);
  assign out = {{15{1'b0}}, or_1_out};  // Bit_Extender bit_extender_1
endmodule

module bc (
  input  [15:0] rs,
  output [15:0] out
);

  wire [4:0] bitadder_1_out;

  BitAdder #(.width(16)) bitadder_1 (.in0(rs), .out(bitadder_1_out));
  assign out = {{11{1'b0}}, bitadder_1_out};  // Bit_Extender bit_extender_1
endmodule

module addi (
  input  [15:0] rs,
  input  [15:0] Imm,
  output [15:0] out
);

  Adder #(.width(16)) adder_1 (.a(rs), .b(Imm), .out(out));  // open: cin, cout
endmodule

module andi (
  input  [15:0] rs,
  input  [15:0] Imm,
  output [15:0] out
);

  assign out = rs & Imm;  // AND_Gate and_1, 16 bits wide
endmodule

module ori (
  input  [15:0] rs,
  input  [15:0] Imm,
  output [15:0] out
);

  assign out = rs | Imm;  // OR_Gate or_1, 16 bits wide
endmodule

module beq (
  input  [15:0] rs,
  input  [15:0] Imm,
  output [15:0] out
);

  wire comparator_1_eq;

  Comparator #(.width(16)) comparator_1 (.a(rs), .b(Imm), .eq(comparator_1_eq));  // open: gt, lt
  assign out = {{15{1'b0}}, comparator_1_eq};  // Bit_Extender bit_extender_1
endmodule

module bne (
  input  [15:0] rs,
  input  [15:0] Imm,
  output [15:0] out
);

  wire comparator_1_eq, not_1_out;

  Comparator #(.width(16)) comparator_1 (.a(rs), .b(Imm), .eq(comparator_1_eq));  // open: gt, lt
  not not_1 (not_1_out, comparator_1_eq);
  assign out = {{15{1'b0}}, not_1_out};  // Bit_Extender bit_extender_1
endmodule
