// Logisim project cpu.circ as structural Verilog: 7 circuits, main circuit main
module main (
  input  [15:0] From_Instr_Mem,
  input  clk,
  output [15:0] r0,
  output [15:0] r1,
  output [15:0] r2,
  output [15:0] r3,
  output [15:0] Display_0,
  output [15:0] Display_1,
  output [15:0] To_Instr_Mem,
  output [15:0] Data_Mem_Data,
  output [15:0] Data_Mem_Addr,
  output Data_Mem_Write
);

  wire _16Addr, ALUSrc, and_1_out, and_2_out, CLEAR_MEM_out, Dsp, eq, jal, Jump, kill, memRead, not_1_out,
       not_2_out, OF, PCSrc, sign, WB;
  wire [1:0] Branch, multiplexer_4_out, RegDst;
  wire [3:0] ALU_Control_out_3;
  wire [15:0] adder_1_out, bit_extender_1_out, bit_extender_2_out, brAddr, currInst, demultiplexer_1_out0,
       demultiplexer_1_out1, memory_1_data_out, multiplexer_1_out, multiplexer_2_out, multiplexer_3_out,
       multiplexer_5_out, multiplexer_6_out, multiplexer_7_out, multiplexer_9_out, multiplexer_10_out,
       Output, rsData, target;

  Multiplexer #(.width(16)) multiplexer_1 (
    .in0(brAddr), .in1(Data_Mem_Addr), .out(multiplexer_1_out), .sel(Jump));  // open: en
  Instruction_Killer instruction_killer_1 (.eq(eq), .Branch(Branch), .Kill(kill));
  Multiplexer #(.width(16)) multiplexer_2 (
    .in0(adder_1_out), .in1(multiplexer_1_out), .out(multiplexer_2_out), .sel(PCSrc));  // open: en
  Multiplexer #(.width(16)) multiplexer_3 (
    .in0(From_Instr_Mem), .in1({16{1'b0}}), .out(multiplexer_3_out), .sel(kill));  // open: en
  Register #(.width(16)) register_1 (.D(multiplexer_2_out), .Q(To_Instr_Mem), .clk(clk));  // open: en, clr
  Adder #(.width(16)) adder_1 (.a(16'h1), .b(To_Instr_Mem), .out(adder_1_out));  // open: cin, cout
  Register #(.width(16)) register_2 (.D(multiplexer_3_out), .Q(currInst), .clk(clk));  // open: en, clr
  Control control_1 (
    .OP(currInst[15:12]), .WB(WB), .ALUSrc(ALUSrc), .RegDst(RegDst), .Branch_Jump(Branch), .Jump(Jump),
    ._16addr(_16Addr), .jal(jal), .memRead(memRead), .memWrite(Data_Mem_Write), .sign(sign), .Display(Dsp));
  Multiplexer #(.select(2), .width(2)) multiplexer_4 (
    .in0(currInst[7:6]), .in1(currInst[9:8]), .in2(2'b11), .out(multiplexer_4_out), .sel(RegDst));  // open: in3, en
  Regfile_main main_1 (
    .Read_register_1(currInst[11:10]), .Read_register_2(currInst[9:8]), .write_register(multiplexer_4_out),
    .write_data(Output), .Reg_0_Value(r0), .Reg_1_Value(r1), .Reg_2_Value(r2), .Reg_3_Value(r3),
    .RegWrite(WB), .clock(clk), .Read_Data_1(rsData), .Read_Data_2(Data_Mem_Data));
  assign bit_extender_1_out = {{8{1'b0}}, currInst[7:0]};  // Bit_Extender bit_extender_1
  assign bit_extender_2_out = {{8{currInst[7]}}, currInst[7:0]};  // Bit_Extender bit_extender_2
  target_Addr target_addr_1 (.From_Instr_Mem(currInst), .nxt_PC(To_Instr_Mem), .target(target));
  Multiplexer #(.width(16)) multiplexer_5 (
    .in0(bit_extender_1_out), .in1(bit_extender_2_out), .out(multiplexer_5_out), .sel(sign));  // open: en
  Adder #(.width(16)) adder_2 (.a(To_Instr_Mem), .b(multiplexer_5_out), .out(brAddr));  // open: cin, cout
  Multiplexer #(.width(16)) multiplexer_6 (
    .in0(rsData), .in1(target), .out(multiplexer_6_out), .sel(_16Addr));  // open: en
  Multiplexer #(.width(16)) multiplexer_7 (
    .in0(Data_Mem_Data), .in1(multiplexer_5_out), .out(multiplexer_7_out), .sel(ALUSrc));  // open: en
  alu_main main_2 (
    .switch__S(ALU_Control_out_3), .X(multiplexer_6_out), .equal(eq), .result(Data_Mem_Addr),
    .signed_overflow(OF), .Y(multiplexer_7_out));
  ALU_Control ALU_Control (.OP(currInst[15:12]), .Func(currInst[3:0]), .out_3(ALU_Control_out_3));
  not not_1 (not_1_out, eq);
  Multiplexer #(.select(2)) multiplexer_8 (
    .in0(1'b0), .in1(eq), .in2(not_1_out), .in3(1'b1), .out(PCSrc), .sel(Branch));  // open: en
  Multiplexer #(.width(16)) multiplexer_9 (
    .in0(rsData), .in1(Data_Mem_Data), .out(multiplexer_9_out), .sel(Data_Mem_Write));  // open: en
  Multiplexer #(.width(16)) multiplexer_10 (
    .in0(Data_Mem_Addr), .in1(To_Instr_Mem), .out(multiplexer_10_out), .sel(jal));  // open: en
  Hex_Digit_Display hex_digit_display_1 (.value(Display_0[11:8]));  // open: dp
  Hex_Digit_Display hex_digit_display_2 (.value(Display_0[15:12]));  // open: dp
  memory memory_1 (
    .Data_In(multiplexer_9_out), .Address(multiplexer_10_out), .clk(clk), .Reset(CLEAR_MEM_out),
    .Data_Out(memory_1_data_out), .MemWrite(Data_Mem_Write));
  Button CLEAR_MEM (.out(CLEAR_MEM_out));
  Demultiplexer #(.width(16), .enable("false")) demultiplexer_1 (
    .out0(demultiplexer_1_out0), .out1(demultiplexer_1_out1), .in(rsData), .sel(currInst[0]));
  Hex_Digit_Display hex_digit_display_3 (.value(Display_0[7:4]));  // open: dp
  Hex_Digit_Display hex_digit_display_4 (.value(Display_0[3:0]));  // open: dp
  Multiplexer #(.width(16)) multiplexer_11 (
    .in0(multiplexer_10_out), .in1(memory_1_data_out), .out(Output), .sel(memRead));  // open: en
  and and_1 (and_1_out, Dsp, not_2_out);
  not not_2 (not_2_out, currInst[0]);
  Hex_Digit_Display hex_digit_display_5 (.value(Display_1[11:8]));  // open: dp
  Hex_Digit_Display hex_digit_display_6 (.value(Display_1[15:12]));  // open: dp
  Register #(.width(16)) d0 (.D(demultiplexer_1_out0), .en(and_1_out), .Q(Display_0), .clk(clk));  // open: clr
  Hex_Digit_Display hex_digit_display_7 (.value(Display_1[3:0]));  // open: dp
  Hex_Digit_Display hex_digit_display_8 (.value(Display_1[7:4]));  // open: dp
  and and_2 (and_2_out, Dsp, currInst[0]);
  LED led_1 (.in(OF));
  Register #(.width(16)) d1 (.D(demultiplexer_1_out1), .en(and_2_out), .Q(Display_1), .clk(clk));  // open: clr

  // Other names for the same wires on the sheet: Addr[15:0] = Data_Mem_Addr; d0[15:0] = Display_0;
  //   d1[15:0] = Display_1; funct[3:0] = currInst[3:0]; imm[7:0] = currInst[7:0]; rd[1:0] = currInst[7:6];
  //   memWrite = Data_Mem_Write; nxtPC[15:0] = To_Instr_Mem; OP[3:0] = currInst[15:12]; rs[1:0] = currInst[11:10];
  //   rt[1:0] = currInst[9:8]; rtData[15:0] = Data_Mem_Data

  // Notes on the sheet:
  //   This is the current PC that you need to send as OUTPUT
  //   This is the instruction that you would receive as INPUT
  //   PIPELINE HERE
  //   This is a CLK that is an INPUT driven from the harness.
  //   Remember, this circuit is loaded from the harness to be tested!
  //   DO NOT CHANGE THE LOCATIONS OF THE INPUTS/OUTPUTS! IF YOU DO SO, YOU NEED TO MAKE SURE THE PINS ARE AT THE RIGHT PLACE!
  //   0 = RD2; 1 = Imm
  //   These are OUTPUTS to the circuit
  //   MAIN CONTROL HERE
  //   0 = rd; 1 = rt; 2 = $r3
  //   ALU CONTROL HERE
  //   BRANCH CONTROL HERE
  //   0; 1 = beq; 2 = bne; 3 = jump
  //   These are OUTPUTS to the circuit
  //   DISPLAY OUTPUT HERE
endmodule

module Control (
  input  [3:0] OP,
  output WB,
  output ALUSrc,
  output [1:0] RegDst,
  output [1:0] Branch_Jump,
  output Jump,
  output _16addr,
  output jal,
  output memRead,
  output memWrite,
  output sign,
  output Display
);

  wire BrAc, comparator_1_eq, comparator_2_eq, comparator_3_eq, comparator_5_eq, comparator_6_eq, or_4_out;

  Comparator #(.width(4)) comparator_1 (.a(OP), .b(4'b0000), .eq(comparator_1_eq));  // open: gt, lt
  Comparator #(.width(4)) comparator_2 (.a(OP), .b(4'b1010), .eq(comparator_2_eq));  // open: gt, lt
  Comparator #(.width(4)) comparator_3 (.a(OP), .b(4'b1011), .eq(comparator_3_eq));  // open: gt, lt
  Comparator #(.width(4)) comparator_4 (.a(OP), .b(4'b0111), .eq(jal));  // open: gt, lt
  Comparator #(.width(4)) comparator_5 (.a(OP), .b(4'b1000), .eq(comparator_5_eq));  // open: gt, lt
  Comparator #(.width(4)) comparator_6 (.a(OP), .b(4'b1001), .eq(comparator_6_eq));  // open: gt, lt
  Comparator #(.width(4)) comparator_7 (.a(OP), .b(4'b1111), .eq(Display));  // open: gt, lt
  or or_1 (Jump, jal, comparator_5_eq, comparator_6_eq);
  or or_2 (_16addr, comparator_5_eq, jal);
  or or_3 (BrAc, comparator_3_eq, comparator_2_eq);
  Multiplexer #(.select(4)) multiplexer_1 (
    .in0(1'b1), .in1(1'b1), .in2(1'b1), .in3(1'b1), .in4(1'b1), .in5(1'b1), .in6(1'b1), .in7(1'b1),
    .in8(1'b0), .in9(1'b0), .in10(1'b0), .in11(1'b0), .in12(1'b0), .in13(1'b1), .in14(1'b1), .in15(1'b0),
    .out(WB), .sel(OP));  // open: en
  or or_4 (or_4_out, comparator_1_eq, comparator_2_eq, comparator_3_eq);
  Multiplexer #(.select(4), .width(2)) multiplexer_2 (
    .in0(2'b00), .in1(2'b01), .in2(2'b01), .in3(2'b01), .in4(2'b01), .in5(2'b01), .in6(2'b01), .in7(2'b10),
    .in8(2'b00), .in9(2'b00), .in10(2'b00), .in11(2'b00), .in12(2'b00), .in13(2'b01), .in14(2'b01),
    .in15(2'b00), .out(RegDst), .sel(OP));  // open: en
  Multiplexer #(.select(4), .width(2)) multiplexer_3 (
    .in0(2'b00), .in1(2'b00), .in2(2'b00), .in3(2'b00), .in4(2'b00), .in5(2'b00), .in6(2'b00), .in7(2'b11),
    .in8(2'b11), .in9(2'b11), .in10(2'b01), .in11(2'b10), .in12(2'b00), .in13(2'b00), .in14(2'b00),
    .in15(2'b00), .out(Branch_Jump), .sel(OP));  // open: en
  not not_1 (ALUSrc, or_4_out);
  Multiplexer #(.select(4)) multiplexer_4 (
    .in0(1'b0), .in1(1'b0), .in2(1'b0), .in3(1'b0), .in4(1'b1), .in5(1'b0), .in6(1'b0), .in7(1'b0),
    .in8(1'b0), .in9(1'b0), .in10(1'b1), .in11(1'b1), .in12(1'b1), .in13(1'b0), .in14(1'b1), .in15(1'b0),
    .out(sign), .sel(OP));  // open: en
  Comparator #(.width(4)) comparator_8 (.a(OP), .b(4'b1110), .eq(memRead));  // open: gt, lt
  Comparator #(.width(4)) comparator_9 (.a(OP), .b(4'b1100), .eq(memWrite));  // open: gt, lt

  // Notes on the sheet:
  //   0 = RD2; 1 = Imm
  //   0 = rd; 1 = rt; 2 = $r3
  //   0; 1 = beq; 2 = bne; 3 = jump
endmodule

module ALU_Control (
  input  [3:0] OP,
  input  [3:0] Func,
  output [3:0] out_3
);

  Multiplexer #(.select(4), .width(4)) multiplexer_1 (
    .in0(Func), .in1(4'b1000), .in2(4'b1001), .in3(4'b1010), .in4(4'b0110), .in5(4'b0000), .in6(4'b0001),
    .in7(4'b1011), .in8(4'b1011), .in9(4'b1011), .in10(4'b0000), .in11(4'b0000), .in12(4'b0110),
    .in13(4'b1100), .in14(4'b0110), .in15(4'b0000), .out(out_3), .sel(OP));  // open: en
endmodule

// target
module target_Addr (
  input  [15:0] From_Instr_Mem,
  input  [15:0] nxt_PC,
  output [15:0] target
);

  wire [15:0] and_1_out, and_2_out, subtractor_1_out;

  Subtractor #(.width(16)) subtractor_1 (.a(nxt_PC), .b(16'h1), .out(subtractor_1_out));  // open: bin, bout
  assign and_1_out = From_Instr_Mem & 16'hfff;  // AND_Gate and_1, 16 bits wide
  assign and_2_out = subtractor_1_out & 16'hf000;  // AND_Gate and_2, 16 bits wide
  assign target = and_1_out | and_2_out;  // OR_Gate or_1, 16 bits wide
endmodule

// mem
module memory (
  input  [15:0] Data_In,
  input  [15:0] Address,
  input  Reset,
  input  clk,
  input  MemWrite,
  output [15:0] Data_Out
);

  wire not_1_out;

  assign Data_Out = MemWrite ? Data_In : 16'bz;  // Controlled_Buffer controlled_buffer_1
  not not_1 (not_1_out, MemWrite);
  RAM #(.addrWidth(16), .dataWidth(16)) ram_1 (
    .addr(Address), .data(Data_Out), .sel(1'b1), .clk(clk), .ld(not_1_out), .clr(Reset));
endmodule

module Display (
  input  [15:0] in_1
);

  Hex_Digit_Display hex_digit_display_1 (.value(in_1[15:12]));  // open: dp
  Hex_Digit_Display hex_digit_display_2 (.value(in_1[7:4]));  // open: dp
  Hex_Digit_Display hex_digit_display_3 (.value(in_1[11:8]));  // open: dp
  Hex_Digit_Display hex_digit_display_4 (.value(in_1[3:0]));  // open: dp
endmodule

// kill
module Instruction_Killer (
  input  eq,
  input  [1:0] Branch,
  output Kill
);

  wire and_1_out, and_2_out, comparator_1_eq, comparator_2_eq, comparator_3_eq, not_1_out, or_1_out;

  Comparator #(.width(2)) comparator_1 (.a(Branch), .b(2'b01), .eq(comparator_1_eq));  // open: gt, lt
  Comparator #(.width(2)) comparator_2 (.a(Branch), .b(2'b10), .eq(comparator_2_eq));  // open: gt, lt
  Comparator #(.width(2)) comparator_3 (.a(Branch), .b(2'b11), .eq(comparator_3_eq));  // open: gt, lt
  not not_1 (not_1_out, eq);
  and and_1 (and_1_out, eq, comparator_1_eq);
  or or_1 (or_1_out, and_1_out, and_2_out);
  and and_2 (and_2_out, not_1_out, comparator_2_eq);
  or or_2 (Kill, or_1_out, comparator_3_eq);
endmodule
