// Logisim project alu_20121108_0212.circ as structural Verilog: 9 circuits, main circuit main
module main (
  input  [15:0] X,
  input  [15:0] Y,
  input  [3:0] switch__S,
  output signed_overflow,
  output [15:0] result,
  output equal
);

  wire adder_1_cout, and_1_out, and_2_out, comparator_1_eq, comparator_2_eq, comparator_3_lt,
       subtractor_1_bout;
  wire [15:0] adder_1_out, and_3_out, bc, ffo, lui, multiplexer_1_out, or_out, shifter_1_out, shifter_2_out,
       shifter_3_out, subtractor_1_out, zb;

  Comparator #(.width(4)) comparator_1 (.a(switch__S), .b(4'b1110), .eq(comparator_1_eq));  // open: gt, lt
  Comparator #(.width(4)) comparator_2 (.a(switch__S), .b(4'b1111), .eq(comparator_2_eq));  // open: gt, lt
  Comparator #(.width(16)) comparator_3 (.a(X), .b(Y), .lt(comparator_3_lt));  // open: gt, eq
  and and_1 (and_1_out, comparator_1_eq, adder_1_cout);
  and and_2 (and_2_out, comparator_2_eq, subtractor_1_bout);
  assign and_3_out = X & Y;  // AND_Gate and_3, 16 bits wide
  assign or_out = X | Y;  // OR_Gate or, 16 bits wide
  Multiplexer #(.width(16)) multiplexer_1 (
    .in0({16{1'b0}}), .in1(16'h1), .out(multiplexer_1_out), .sel(comparator_3_lt));  // open: en
  Shifter #(.width(16)) shifter_1 (.in(X), .\dist (Y[3:0]), .out(shifter_1_out));
  Shifter #(.width(16), .shift("lr")) shifter_2 (.in(X), .\dist (Y[3:0]), .out(shifter_2_out));
  Shifter #(.width(16), .shift("ar")) shifter_3 (.in(X), .\dist (Y[3:0]), .out(shifter_3_out));
  Adder #(.width(16)) adder_1 (.a(X), .b(Y), .out(adder_1_out), .cout(adder_1_cout));  // open: cin
  Subtractor #(.width(16)) subtractor_1 (.a(X), .b(Y), .out(subtractor_1_out), .bout(subtractor_1_bout));  // open: bin
  Comparator #(.width(16)) comparator_4 (.a(X), .b(Y), .eq(equal));  // open: gt, lt
  or or_2 (signed_overflow, and_1_out, and_2_out);
  Multiplexer #(.select(4), .width(16)) multiplexer_2 (
    .in0(and_3_out), .in1(or_out), .in2(multiplexer_1_out), .in3(shifter_1_out), .in4(shifter_2_out),
    .in5(shifter_3_out), .in6(adder_1_out), .in7(subtractor_1_out), .in8(ffo), .in9(zb), .in10(bc), .in11(X),
    .in12(lui), .out(result), .sel(switch__S));  // open: in13, in14, in15, en
  ffo u_ffo (.rs(X), .out(ffo));
  zb u_zb (.rs(X), .out(zb));
  bc u_bc (.rs(X), .out(bc));
  Shifter #(.width(16)) shifter_4 (.in(Y), .\dist (4'b1000), .out(lui));

  // Other names for the same wires on the sheet: j[15:0] = X; S[3:0] = switch__S

  // Notes on the sheet:
  //   These are INPUTS to your circuit
  //   This is an INPUT to your circuit
  //   DO NOT CHANGE THE LOCATIONS OF THE INPUTS/OUTPUTS! IF YOU DO SO, YOU NEED TO MAKE SURE THE PINS ARE AT THE RIGHT PLACE!
  //   These are OUTPUTS to your circuit
endmodule

module ffo (
  input  [15:0] rs,
  output [15:0] out
);

  wire bitfinder_1_found;
  wire [3:0] bitfinder_1_index;
  wire [15:0] bit_extender_1_out, subtractor_1_out;

  BitFinder #(.width(16), .\type ("high1")) bitfinder_1 (.in(rs), .index(bitfinder_1_index), .found(bitfinder_1_found));
  Subtractor #(.width(16)) subtractor_1 (.a(16'hf), .b(bit_extender_1_out), .out(subtractor_1_out));  // open: bin, bout
  assign bit_extender_1_out = {{12{1'b0}}, bitfinder_1_index};  // Bit_Extender bit_extender_1
  Multiplexer #(.width(16)) multiplexer_1 (
    .in0(16'h10), .in1(subtractor_1_out), .out(out), .sel(bitfinder_1_found));  // open: en
endmodule

module zb (
  input  [15:0] rs,
  output [15:0] out
);

  wire comparator_1_eq, comparator_2_eq, comparator_3_eq, comparator_4_eq, or_1_out;

  Comparator #(.width(4)) comparator_1 (.a(rs[3:0]), .b(4'b0000), .eq(comparator_1_eq));  // open: gt, lt
  Comparator #(.width(4)) comparator_2 (.a(rs[7:4]), .b(4'b0000), .eq(comparator_2_eq));  // open: gt, lt
  Comparator #(.width(4)) comparator_3 (.a(rs[11:8]), .b(4'b0000), .eq(comparator_3_eq));  // open: gt, lt
  Comparator #(.width(4)) comparator_4 (.a(rs[15:12]), .b(4'b0000), .eq(comparator_4_eq));  // open: gt, lt
  or or_1 (or_1_out, comparator_1_eq, comparator_2_eq, comparator_3_eq, comparator_4_eq);
  assign out = {{15{1'b0}}, or_1_out};  // Bit_Extender bit_extender_1
endmodule

module bc (
  input  [15:0] rs,
  output [15:0] out
);

  wire [4:0] bitadder_1_out;

  BitAdder #(.width(16)) bitadder_1 (.in0(rs), .out(bitadder_1_out));
  assign out = {{11{1'b0}}, bitadder_1_out};  // Bit_Extender bit_extender_1
endmodule

module addi (
  input  [15:0] rs,
  input  [15:0] Imm,
  output [15:0] out
);

  Adder #(.width(16)) adder_1 (.a(rs), .b(Imm), .out(out));  // open: cin, cout
endmodule

module andi (
  input  [15:0] rs,
  input  [15:0] Imm,
  output [15:0] out
);

  assign out = rs & Imm;  // AND_Gate and_1, 16 bits wide
endmodule

module ori (
  input  [15:0] rs,
  input  [15:0] Imm,
  output [15:0] out
);

  assign out = rs | Imm;  // OR_Gate or_1, 16 bits wide
endmodule

module beq (
  input  [15:0] rs,
  input  [15:0] Imm,
  output [15:0] out
);

  wire comparator_1_eq;

  Comparator #(.width(16)) comparator_1 (.a(rs), .b(Imm), .eq(comparator_1_eq));  // open: gt, lt
  assign out = {{15{1'b0}}, comparator_1_eq};  // Bit_Extender bit_extender_1
endmodule

module bne (
  input  [15:0] rs,
  input  [15:0] Imm,
  output [15:0] out
);

  wire comparator_1_eq, not_1_out;

  Comparator #(.width(16)) comparator_1 (.a(rs), .b(Imm), .eq(comparator_1_eq));  // open: gt, lt
  not not_1 (not_1_out, comparator_1_eq);
  assign out = {{15{1'b0}}, not_1_out};  // Bit_Extender bit_extender_1
endmodule
