// Logisim project Regfile.circ as structural Verilog: 1 circuit, main circuit main
module main (
  input  [1:0] Read_register_1,
  input  [1:0] Read_register_2,
  input  [1:0] write_register,
  input  [15:0] write_data,
  input  RegWrite,
  input  clock,
  output [15:0] Reg_0_Value,
  output [15:0] Reg_1_Value,
  output [15:0] Reg_2_Value,
  output [15:0] Reg_3_Value,
  output [15:0] Read_Data_1,
  output [15:0] Read_Data_2
);

  wire R1, R2, R3, R4;
  wire [15:0] multiplexer_1_out, w1, w2, w3, w4;

  Comparator #(.width(2)) comparator_1 (.a(write_register), .b(2'b00), .eq(R1));  // open: gt, lt
  Comparator #(.width(2)) comparator_2 (.a(write_register), .b(2'b01), .eq(R2));  // open: gt, lt
  Comparator #(.width(2)) comparator_3 (.a(write_register), .b(2'b10), .eq(R3));  // open: gt, lt
  Comparator #(.width(2)) comparator_4 (.a(write_register), .b(2'b11), .eq(R4));  // open: gt, lt
  Multiplexer #(.width(16)) multiplexer_1 (.in1(write_data), .out(multiplexer_1_out), .sel(RegWrite));  // open: in0, en
  Register #(.width(16)) register_1 (.D(w1), .en(R1), .Q(Reg_0_Value), .clk(clock));  // open: clr
  Register #(.width(16)) register_2 (.D(w2), .en(R2), .Q(Reg_1_Value), .clk(clock));  // open: clr
  Multiplexer #(.select(2), .width(16)) multiplexer_2 (
    .in0(Reg_0_Value), .in1(Reg_1_Value), .in2(Reg_2_Value), .in3(Reg_3_Value), .out(Read_Data_1),
    .sel(Read_register_1));  // open: en
  Multiplexer #(.select(2), .width(16)) multiplexer_3 (
    .in0(Reg_0_Value), .in1(Reg_1_Value), .in2(Reg_2_Value), .in3(Reg_3_Value), .out(Read_Data_2),
    .sel(Read_register_2));  // open: en
  Demultiplexer #(.select(2), .width(16)) demultiplexer_1 (
    .out0(w1), .out1(w2), .out2(w3), .out3(w4), .in(multiplexer_1_out), .sel(write_register));  // open: en
  Register #(.width(16)) register_3 (.D(w3), .en(R3), .Q(Reg_2_Value), .clk(clock));  // open: clr
  Register #(.width(16)) register_4 (.D(w4), .en(R4), .Q(Reg_3_Value), .clk(clock));  // open: clr

  // Other names for the same wires on the sheet: WR[1:0] = write_register

  // Notes on the sheet:
  //   These are INPUTS to the circuit
  //   These are INPUTS to the circuit
  //   DO NOT CHANGE THE LOCATIONS OF THE INPUTS/OUTPUTS! IF YOU DO SO, YOU NEED TO MAKE SURE THE PINS ARE AT THE RIGHT PLACE!
  //   These are OUTPUTS to the circuit
  //   Yet again, the clock is not an actual clock, but an input, one that will should/will be inputed from the higher circuit
  //   These are OUTPUTS to the circuit
endmodule
